// Logisim project LockController_ExtraCredit.circ as structural Verilog: 4 circuits, main circuit LockController
module LockController (
  input  CLK,
  input  RST,
  input  K0,
  input  K1,
  input  K2,
  input  K3,
  input  K4,
  input  K5,
  input  K6,
  input  K7,
  input  K8,
  input  K9,
  input  KS,
  input  KL,
  input  KU,
  input  KP,
  output LEDB,
  output LEDR,
  output LOCK_ACT,
  output LOCK_CMD
);

  wire key_detection_invalid, key_detection_k0_valid, key_detection_k1_valid, key_detection_k2_valid,
       key_detection_k3_valid, key_detection_k4_valid, key_detection_k5_valid, key_detection_k6_valid,
       key_detection_k7_valid, key_detection_k8_valid, key_detection_k9_valid, key_detection_kl_valid,
       key_detection_kp_valid, key_detection_ks_valid, key_detection_ku_valid, key_detection_match,
       key_detection_no_key, lock_fsm_correct;
  wire [3:0] lock_fsm_new1, lock_fsm_new2, lock_fsm_new3;

  ec_key_detect key_detection (
    .CLK(CLK), .in_2({KP, KU, KL, KS, K9, K8, K7, K6, K5, K4, K3, K2, K1, K0}), .NEW3(lock_fsm_new3),
    .NEW2(lock_fsm_new2), .NEW1(lock_fsm_new1), .CORRECT(lock_fsm_correct), .RST(RST),
    .match(key_detection_match), .K0_VALID(key_detection_k0_valid), .K1_VALID(key_detection_k1_valid),
    .K2_VALID(key_detection_k2_valid), .K3_VALID(key_detection_k3_valid), .K4_VALID(key_detection_k4_valid),
    .K5_VALID(key_detection_k5_valid), .K6_VALID(key_detection_k6_valid), .K7_VALID(key_detection_k7_valid),
    .K8_VALID(key_detection_k8_valid), .K9_VALID(key_detection_k9_valid), .KS_VALID(key_detection_ks_valid),
    .KL_VALID(key_detection_kl_valid), .KU_VALID(key_detection_ku_valid), .KP_VALID(key_detection_kp_valid),
    .INVALID(key_detection_invalid), .NO_KEY(key_detection_no_key));
  ec_fsm_neat lock_fsm (
    .CLK(CLK), .RST(RST), .match(key_detection_match), .K0(key_detection_k0_valid),
    .K1(key_detection_k1_valid), .K2(key_detection_k2_valid), .K3(key_detection_k3_valid),
    .K4(key_detection_k4_valid), .K5(key_detection_k5_valid), .K6(key_detection_k6_valid),
    .K7(key_detection_k7_valid), .K8(key_detection_k8_valid), .K9(key_detection_k9_valid),
    .KS(key_detection_ks_valid), .KL(key_detection_kl_valid), .KU(key_detection_ku_valid),
    .KP(key_detection_kp_valid), .INVALID(key_detection_invalid), .NO_KEY(key_detection_no_key),
    .CORRECT(lock_fsm_correct), .NEW1(lock_fsm_new1), .NEW2(lock_fsm_new2), .NEW3(lock_fsm_new3),
    .LOCK_CMD(LOCK_CMD), .LOCK_ACT(LOCK_ACT), .LEDR(LEDR), .LEDB(LEDB));
endmodule

module ec_FSM (
  input  CLK,
  input  RST,
  input  match,
  input  K0,
  input  K1,
  input  K2,
  input  K3,
  input  K4,
  input  K5,
  input  K6,
  input  K7,
  input  K8,
  input  K9,
  input  KS,
  input  KL,
  input  KU,
  input  KP,
  input  INVALID,
  input  NO_KEY,
  output CORRECT,
  output [3:0] NEW1,
  output [3:0] NEW2,
  output [3:0] NEW3,
  output LOCK_CMD,
  output LOCK_ACT,
  output LEDR,
  output LEDB
);

  wire and_1_out, and_2_out, and_3_out, and_4_out, and_5_out, and_6_out, and_7_out, and_8_out, and_9_out,
       and_10_out, and_11_out, and_12_out, and_14_out, and_15_out, and_16_out, and_17_out, and_18_out,
       and_19_out, and_20_out, and_21_out, and_22_out, and_23_out, and_24_out, and_28_out, and_29_out,
       and_30_out, and_31_out, and_32_out, and_33_out, and_34_out, and_35_out, and_36_out, and_37_out,
       and_38_out, and_39_out, and_40_out, and_41_out, and_42_out, and_43_out, and_44_out, and_45_out,
       and_46_out, and_47_out, and_48_out, and_49_out, and_50_out, and_51_out, and_52_out, and_53_out,
       b1_u_match_out, b_prime___u_out, comparator_1_eq, comparator_2_eq, comparator_3_eq, comparator_4_eq,
       comparator_5_eq, comparator_6_eq, comparator_7_eq, comparator_8_eq, comparator_9_eq, FAIL, FAIL2,
       FAIL3, K, NS0, NS1_q, NS2_q, NS3_q, NS4_q, NS5, NS5_17, NS6, NS7, NS8, NS9, NS10, NS11, NS12, NS13,
       NS14, NS15, NS16, NS17, NS18, or_1_out, or_2_out, or_4_out, or_5_out, or_6_out, or_7_out, or_8_out,
       or_9_out, or_10_out, or_11_out, or_12_out, or_13_out, or_14_out, or_15_out, or_16_out, or_18_out,
       or_19_out, or_20_out, or_24_out, or_25_out, or_27_out, or_28_out, or_29_out, or_30_out, or_31_out,
       or_32_out, or_33_out, or_34_out, or_35_out, or_36_out, or_37_out, or_38_out, or_39_out, SCS,
       u_match_prime_out;
  wire [3:0] multiplexer_1_out, priority_encoder_1_out, shift_register_1_q0, shift_register_1_q1,
       shift_register_1_q2, shift_register_1_q3, shift_register_1_q4, shift_register_1_q5,
       shift_register_2_q0, shift_register_2_q1, shift_register_2_q2, undriven, undriven_2, undriven_3,
       undriven_4, undriven_5, undriven_6;

  Priority_Encoder #(.select(4)) priority_encoder_1 (
    .in0(K0), .in1(K1), .in2(K2), .in3(K3), .in4(K4), .in5(K5), .in6(K6), .in7(K7), .in8(K8), .in9(K9),
    .in10(KS), .in11(KL), .in12(KU), .in13(KP), .in14(INVALID), .in15(NO_KEY), .out(priority_encoder_1_out));  // open: gs, en_out, en_in
  or or_1 (or_1_out, NS11, NS12, NS13);
  and and_1 (and_1_out, or_1_out, K);
  or or_2 (or_2_out, NS14, NS15, NS16);
  and and_2 (and_2_out, or_2_out, K);
  or or_3 (K, K0, K1, K2, K3, K4, K5, K6, K7, K8, K9);
  Multiplexer #(.select(4), .width(4)) multiplexer_1 (
    .in0(4'b0000), .in1(4'b0001), .in2(4'b0010), .in3(4'b0011), .in4(4'b0100), .in5(4'b0101), .in6(4'b0110),
    .in7(4'b0111), .in8(4'b1000), .in9(4'b1001), .in10(undriven), .in11(undriven_4), .in12(undriven_2),
    .in13(undriven_5), .in14(undriven_3), .in15(undriven_6), .out(multiplexer_1_out),
    .sel(priority_encoder_1_out));  // open: en
  or or_4 (or_4_out, INVALID, NO_KEY);
  or or_5 (or_5_out, NS5, NS6, NS7, NS8, NS9, NS10);
  Shift_Register #(.width(4), .length(6)) shift_register_1 (
    .shift(and_5_out), .in(multiplexer_1_out), .clk(CLK), .q0(shift_register_1_q0), .q1(shift_register_1_q1),
    .q2(shift_register_1_q2), .q3(shift_register_1_q3), .q4(shift_register_1_q4), .q5(shift_register_1_q5));  // open: out, load, clr, d0, d1, d2, d3, d4, d5
  Shift_Register #(.width(4), .length(3)) shift_register_2 (
    .shift(and_1_out), .in(multiplexer_1_out), .clk(CLK), .q0(shift_register_2_q0), .q1(shift_register_2_q1),
    .q2(shift_register_2_q2));  // open: out, load, clr, d0, d1, d2
  Shift_Register #(.width(4), .length(3)) shift_register_3 (
    .shift(and_2_out), .in(multiplexer_1_out), .clk(CLK), .q0(NEW3), .q1(NEW2), .q2(NEW1));  // open: out, load, clr, d0, d1, d2
  and and_3 (and_3_out, NS4_q, ~KS);  // AND_Gate
  and and_4 (and_4_out, NS3_q, ~KS);  // AND_Gate
  and and_5 (and_5_out, or_5_out, K);
  and u_match_prime (u_match_prime_out, KU, ~match);  // AND_Gate
  and and_6 (and_6_out, NS2_q, ~KS);  // AND_Gate
  or or_6 (or_6_out, NO_KEY, INVALID, K, ~KS);  // OR_Gate
  or or_7 (or_7_out, NO_KEY, INVALID, K, KS);
  or or_8 (or_8_out, NS0, NS1_q);
  Comparator #(.width(4), .mode("unsigned")) comparator_1 (
    .a(shift_register_1_q5), .b(4'b0001), .eq(comparator_1_eq));  // open: gt, lt
  Comparator #(.width(4), .mode("unsigned")) comparator_2 (
    .a(shift_register_1_q4), .b(4'b0110), .eq(comparator_2_eq));  // open: gt, lt
  Comparator #(.width(4), .mode("unsigned")) comparator_3 (
    .a(shift_register_1_q3), .b(4'b0001), .eq(comparator_3_eq));  // open: gt, lt
  Comparator #(.width(4), .mode("unsigned")) comparator_4 (
    .a(shift_register_1_q2), .b(4'b1000), .eq(comparator_4_eq));  // open: gt, lt
  Comparator #(.width(4), .mode("unsigned")) comparator_5 (
    .a(shift_register_1_q1), .b(4'b0000), .eq(comparator_5_eq));  // open: gt, lt
  Comparator #(.width(4), .mode("unsigned")) comparator_6 (
    .a(shift_register_1_q0), .b(4'b0011), .eq(comparator_6_eq));  // open: gt, lt
  Comparator #(.width(4), .mode("unsigned")) comparator_7 (
    .a(shift_register_2_q2), .b(NEW1), .eq(comparator_7_eq));  // open: gt, lt
  Comparator #(.width(4), .mode("unsigned")) comparator_8 (
    .a(shift_register_2_q1), .b(NEW2), .eq(comparator_8_eq));  // open: gt, lt
  Comparator #(.width(4), .mode("unsigned")) comparator_9 (
    .a(shift_register_2_q0), .b(NEW3), .eq(comparator_9_eq));  // open: gt, lt
  or or_9 (or_9_out, u_match_prime_out, KP, KL);
  and and_7 (and_7_out, NS3_q, or_6_out);
  and and_8 (and_8_out, or_7_out, or_8_out);
  or or_10 (or_10_out, NS5, NS6, NS7, NS8, NS9, NS10, NS11, NS12, NS13, NS14, NS15, NS16);
  and and_9 (and_9_out, comparator_1_eq, comparator_2_eq, comparator_3_eq, comparator_4_eq, comparator_5_eq, comparator_6_eq);
  and and_10 (and_10_out, comparator_7_eq, comparator_8_eq, comparator_9_eq);
  and b1_u_match (b1_u_match_out, match, KU, NS1_q);
  and and_11 (and_11_out, or_9_out, NS1_q);
  and b_prime___u (b_prime___u_out, KU, NS0);
  and b0_L (LOCK_CMD, KL, NS0);
  or or_11 (or_11_out, NS1_q, NS0);
  and and_12 (and_12_out, NS0, or_4_out);
  and and_13 (CORRECT, and_9_out, and_10_out);
  and and_14 (and_14_out, NS4_q, or_4_out);
  and and_15 (and_15_out, K, or_11_out);
  or or_12 (or_12_out, KS, and_12_out);
  and and_16 (and_16_out, or_25_out, KS);
  or or_13 (or_13_out, NS0, NS18, NS5_17);
  or or_14 (or_14_out, and_3_out, and_14_out, b1_u_match_out);
  and and_17 (and_17_out, NS3_q, or_4_out);
  or or_15 (or_15_out, and_11_out, and_4_out, FAIL3, and_17_out, b_prime___u_out);
  and and_18 (and_18_out, NS2_q, or_4_out);
  and and_19 (and_19_out, NS1_q, or_4_out);
  or or_16 (or_16_out, and_19_out, and_15_out);
  and and_20 (and_20_out, or_13_out, ~KP);  // AND_Gate
  or or_17 (NS5_17, NS5, NS6, NS7, NS8, NS9, NS10, NS11, NS12, NS13, NS14, NS15, NS16, NS17);
  or or_18 (or_18_out, KU, INVALID, KL);
  or or_19 (or_19_out, or_10_out, NS18);
  or or_20 (or_20_out, RST, and_6_out, and_18_out, LOCK_CMD, SCS);
  and and_21 (and_21_out, NS17, K);
  and and_22 (and_22_out, NS17, K);
  and and_23 (and_23_out, NS5_17, or_18_out);
  and and_24 (and_24_out, NS18, NO_KEY);
  and and_25 (FAIL2, or_19_out, KP);
  and and_26 (FAIL, NS17, KP, ~CORRECT);  // AND_Gate
  and and_27 (SCS, KP, NS17, CORRECT);
  D_Flip_Flop NS4 (.clk(CLK), .D(or_14_out), .Q(NS4_q));  // open: Qn, preset, en, reset
  D_Flip_Flop NS3 (.clk(CLK), .D(or_15_out), .Q(NS3_q));  // open: Qn, preset, en, reset
  D_Flip_Flop NS2 (.clk(CLK), .D(or_20_out), .Q(NS2_q));  // open: Qn, preset, en, reset
  D_Flip_Flop NS1 (.clk(CLK), .D(or_16_out), .Q(NS1_q));  // open: Qn, preset, en, reset
  D_Flip_Flop u_NS0 (.clk(CLK), .D(or_12_out), .Q(NS0));  // open: Qn, preset, en, reset
  or or_21 (LOCK_ACT, LOCK_CMD, b1_u_match_out);
  or or_22 (LEDR, b_prime___u_out, FAIL2, and_11_out, FAIL, and_7_out);
  or or_23 (LEDB, and_16_out, and_20_out, and_21_out, and_8_out);
  or or_24 (or_24_out, and_23_out, and_22_out, and_24_out);
  or or_25 (or_25_out, NS4_q, NS3_q, NS2_q);
  D_Flip_Flop u_NS18 (.clk(CLK), .D(or_24_out), .Q(NS18));  // open: Qn, preset, en, reset
  or or_26 (FAIL3, FAIL2, FAIL);
  and and_28 (and_28_out, NS0, KP);
  and and_29 (and_29_out, NS5, K);
  and and_30 (and_30_out, NS6, K);
  and and_31 (and_31_out, NS7, K);
  and and_32 (and_32_out, NS8, K);
  and and_33 (and_33_out, NS9, K);
  and and_34 (and_34_out, NS10, K);
  and and_35 (and_35_out, NS11, K);
  and and_36 (and_36_out, NS12, K);
  and and_37 (and_37_out, NS13, K);
  and and_38 (and_38_out, NS14, K);
  and and_39 (and_39_out, NS15, K);
  and and_40 (and_40_out, NS16, K);
  or or_27 (or_27_out, and_28_out, and_41_out);
  and and_41 (and_41_out, NS5, NO_KEY);
  or or_28 (or_28_out, and_29_out, and_42_out);
  and and_42 (and_42_out, NS6, NO_KEY);
  or or_29 (or_29_out, and_30_out, and_43_out);
  and and_43 (and_43_out, NS7, NO_KEY);
  or or_30 (or_30_out, and_31_out, and_44_out);
  and and_44 (and_44_out, NS8, NO_KEY);
  or or_31 (or_31_out, and_32_out, and_45_out);
  and and_45 (and_45_out, NS9, NO_KEY);
  or or_32 (or_32_out, and_33_out, and_46_out);
  and and_46 (and_46_out, NS10, NO_KEY);
  or or_33 (or_33_out, and_34_out, and_47_out);
  and and_47 (and_47_out, NS11, NO_KEY);
  or or_34 (or_34_out, and_35_out, and_48_out);
  and and_48 (and_48_out, NS12, NO_KEY);
  or or_35 (or_35_out, and_36_out, and_49_out);
  and and_49 (and_49_out, NS13, NO_KEY);
  or or_36 (or_36_out, and_37_out, and_50_out);
  and and_50 (and_50_out, NS14, NO_KEY);
  or or_37 (or_37_out, and_38_out, and_51_out);
  and and_51 (and_51_out, NS15, NO_KEY);
  or or_38 (or_38_out, and_39_out, and_52_out);
  and and_52 (and_52_out, NS16, NO_KEY);
  or or_39 (or_39_out, and_40_out, and_53_out);
  and and_53 (and_53_out, NS17, NO_KEY);
  D_Flip_Flop u_NS5 (.clk(CLK), .D(or_27_out), .Q(NS5));  // open: Qn, preset, en, reset
  D_Flip_Flop u_NS6 (.clk(CLK), .D(or_28_out), .Q(NS6));  // open: Qn, preset, en, reset
  D_Flip_Flop u_NS7 (.clk(CLK), .D(or_29_out), .Q(NS7));  // open: Qn, preset, en, reset
  D_Flip_Flop u_NS8 (.clk(CLK), .D(or_30_out), .Q(NS8));  // open: Qn, preset, en, reset
  D_Flip_Flop u_NS9 (.clk(CLK), .D(or_31_out), .Q(NS9));  // open: Qn, preset, en, reset
  D_Flip_Flop u_NS10 (.clk(CLK), .D(or_32_out), .Q(NS10));  // open: Qn, preset, en, reset
  D_Flip_Flop u_NS11 (.clk(CLK), .D(or_33_out), .Q(NS11));  // open: Qn, preset, en, reset
  D_Flip_Flop u_NS12 (.clk(CLK), .D(or_34_out), .Q(NS12));  // open: Qn, preset, en, reset
  D_Flip_Flop u_NS13 (.clk(CLK), .D(or_35_out), .Q(NS13));  // open: Qn, preset, en, reset
  D_Flip_Flop u_NS14 (.clk(CLK), .D(or_36_out), .Q(NS14));  // open: Qn, preset, en, reset
  D_Flip_Flop u_NS15 (.clk(CLK), .D(or_37_out), .Q(NS15));  // open: Qn, preset, en, reset
  D_Flip_Flop u_NS16 (.clk(CLK), .D(or_38_out), .Q(NS16));  // open: Qn, preset, en, reset
  D_Flip_Flop u_NS17 (.clk(CLK), .D(or_39_out), .Q(NS17));  // open: Qn, preset, en, reset

  // Other names for the same wires on the sheet: _0 = K0; _1 = K1; _2 = K2; _3 = K3; _4 = K4; _5 = K5; _6 = K6;
  //   _7 = K7; _8 = K8; _9 = K9; L = KL; P = KP; S = KS; U = KU
endmodule

module ec_key_detect (
  input  CLK,
  input  [13:0] in_2,
  input  [3:0] NEW3,
  input  [3:0] NEW2,
  input  [3:0] NEW1,
  input  CORRECT,
  input  RST,
  output match,
  output K0_VALID,
  output K1_VALID,
  output K2_VALID,
  output K3_VALID,
  output K4_VALID,
  output K5_VALID,
  output K6_VALID,
  output K7_VALID,
  output K8_VALID,
  output K9_VALID,
  output KS_VALID,
  output KL_VALID,
  output KU_VALID,
  output KP_VALID,
  output INVALID,
  output NO_KEY
);

  wire and_1_out, and_2_out, and_3_out, and_4_out, and_5_out, and_6_out, and_7_out, and_8_out, and_9_out,
       and_10_out, and_11_out, and_12_out, and_13_out, and_14_out, comparator_1_gt, comparator_2_eq,
       comparator_3_eq, comparator_4_eq, d_ff_1_q, d_ff_2_q, d_ff_3_q, d_ff_4_q, d_ff_5_q, d_ff_6_q,
       d_ff_7_q, d_ff_8_q, d_ff_9_q, d_ff_10_q, d_ff_11_q, d_ff_12_q, d_ff_13_q, d_ff_14_q, nor_1_out,
       or_1_out, or_2_out, or_3_out, x_2_out, x_3_out, x_4_out, x_5_out, x_6_out, x_7_out, x_8_out, x_9_out,
       x_10_out, x_11_out, x_12_out, x_13_out, x_14_out, x_out;
  wire [3:0] bitadder_1_out, multiplexer_1_out, multiplexer_2_out, multiplexer_3_out, multiplexer_4_out,
       priority_encoder_1_out, register_1_q, register_2_q, register_3_q, shift_register_1_q0,
       shift_register_1_q1, shift_register_1_q2, shift_register_2_q0, shift_register_2_q1,
       shift_register_2_q2, undriven, undriven_2, undriven_3, undriven_4, undriven_5, undriven_6;

  BitAdder #(.width(1)) bitadder_1 (
    .in0(in_2[0]), .in1(in_2[1]), .in2(in_2[2]), .in3(in_2[3]), .in4(in_2[4]), .in5(in_2[5]), .in6(in_2[6]),
    .in7(in_2[7]), .in8(in_2[8]), .in9(in_2[9]), .in10(in_2[10]), .in11(in_2[11]), .in12(in_2[12]),
    .in13(in_2[13]), .out(bitadder_1_out));
  or x (x_out, in_2[1], in_2[2], in_2[3], in_2[4], in_2[5], in_2[6], in_2[7], in_2[8], in_2[9], in_2[10], in_2[11], in_2[12], in_2[13]);
  or x_2 (x_2_out, in_2[0], in_2[2], in_2[3], in_2[4], in_2[5], in_2[6], in_2[7], in_2[8], in_2[9], in_2[10], in_2[11], in_2[12], in_2[13]);
  or x_3 (x_3_out, in_2[1], in_2[0], in_2[3], in_2[4], in_2[5], in_2[6], in_2[7], in_2[8], in_2[9], in_2[10], in_2[11], in_2[12], in_2[13]);
  or x_4 (x_4_out, in_2[1], in_2[2], in_2[0], in_2[4], in_2[5], in_2[6], in_2[7], in_2[8], in_2[9], in_2[10], in_2[11], in_2[12], in_2[13]);
  or x_5 (x_5_out, in_2[1], in_2[2], in_2[3], in_2[0], in_2[5], in_2[6], in_2[7], in_2[8], in_2[9], in_2[10], in_2[11], in_2[12], in_2[13]);
  or x_6 (x_6_out, in_2[1], in_2[2], in_2[3], in_2[4], in_2[0], in_2[6], in_2[7], in_2[8], in_2[9], in_2[10], in_2[11], in_2[12], in_2[13]);
  or x_7 (x_7_out, in_2[1], in_2[2], in_2[3], in_2[4], in_2[5], in_2[0], in_2[7], in_2[8], in_2[9], in_2[10], in_2[11], in_2[12], in_2[13]);
  or x_8 (x_8_out, in_2[1], in_2[2], in_2[3], in_2[4], in_2[5], in_2[6], in_2[0], in_2[8], in_2[9], in_2[10], in_2[11], in_2[12], in_2[13]);
  or x_9 (x_9_out, in_2[1], in_2[2], in_2[3], in_2[4], in_2[5], in_2[6], in_2[7], in_2[0], in_2[9], in_2[10], in_2[11], in_2[12], in_2[13]);
  or x_10 (x_10_out, in_2[1], in_2[2], in_2[3], in_2[4], in_2[5], in_2[6], in_2[7], in_2[8], in_2[0], in_2[10], in_2[11], in_2[12], in_2[13]);
  or x_11 (x_11_out, in_2[1], in_2[2], in_2[3], in_2[4], in_2[5], in_2[6], in_2[7], in_2[8], in_2[9], in_2[0], in_2[11], in_2[12], in_2[13]);
  or x_12 (x_12_out, in_2[1], in_2[2], in_2[3], in_2[4], in_2[5], in_2[6], in_2[7], in_2[8], in_2[9], in_2[10], in_2[0], in_2[12], in_2[13]);
  or x_13 (x_13_out, in_2[1], in_2[2], in_2[3], in_2[4], in_2[5], in_2[6], in_2[7], in_2[8], in_2[9], in_2[10], in_2[11], in_2[0], in_2[13]);
  or x_14 (x_14_out, in_2[1], in_2[2], in_2[3], in_2[4], in_2[5], in_2[6], in_2[7], in_2[8], in_2[9], in_2[10], in_2[11], in_2[12], in_2[0]);
  and and_1 (and_1_out, in_2[0], ~x_out);  // AND_Gate
  and and_2 (and_2_out, in_2[1], ~x_2_out);  // AND_Gate
  and and_3 (and_3_out, in_2[2], ~x_3_out);  // AND_Gate
  and and_4 (and_4_out, in_2[3], ~x_4_out);  // AND_Gate
  and and_5 (and_5_out, in_2[4], ~x_5_out);  // AND_Gate
  and and_6 (and_6_out, in_2[5], ~x_6_out);  // AND_Gate
  and and_7 (and_7_out, in_2[6], ~x_7_out);  // AND_Gate
  and and_8 (and_8_out, in_2[7], ~x_8_out);  // AND_Gate
  and and_9 (and_9_out, in_2[8], ~x_9_out);  // AND_Gate
  and and_10 (and_10_out, in_2[9], ~x_10_out);  // AND_Gate
  and and_11 (and_11_out, in_2[10], ~x_11_out);  // AND_Gate
  and and_12 (and_12_out, in_2[11], ~x_12_out);  // AND_Gate
  and and_13 (and_13_out, in_2[12], ~x_13_out);  // AND_Gate
  and and_14 (and_14_out, in_2[13], ~x_14_out);  // AND_Gate
  D_Flip_Flop d_ff_1 (.clk(CLK), .D(and_1_out), .Q(d_ff_1_q));  // open: Qn, preset, en, reset
  D_Flip_Flop d_ff_2 (.clk(CLK), .D(and_2_out), .Q(d_ff_2_q));  // open: Qn, preset, en, reset
  D_Flip_Flop d_ff_3 (.clk(CLK), .D(and_3_out), .Q(d_ff_3_q));  // open: Qn, preset, en, reset
  D_Flip_Flop d_ff_4 (.clk(CLK), .D(and_4_out), .Q(d_ff_4_q));  // open: Qn, preset, en, reset
  D_Flip_Flop d_ff_5 (.clk(CLK), .D(and_5_out), .Q(d_ff_5_q));  // open: Qn, preset, en, reset
  D_Flip_Flop d_ff_6 (.clk(CLK), .D(and_6_out), .Q(d_ff_6_q));  // open: Qn, preset, en, reset
  D_Flip_Flop d_ff_7 (.clk(CLK), .D(and_7_out), .Q(d_ff_7_q));  // open: Qn, preset, en, reset
  D_Flip_Flop d_ff_8 (.clk(CLK), .D(and_8_out), .Q(d_ff_8_q));  // open: Qn, preset, en, reset
  D_Flip_Flop d_ff_9 (.clk(CLK), .D(and_9_out), .Q(d_ff_9_q));  // open: Qn, preset, en, reset
  D_Flip_Flop d_ff_10 (.clk(CLK), .D(and_10_out), .Q(d_ff_10_q));  // open: Qn, preset, en, reset
  D_Flip_Flop d_ff_11 (.clk(CLK), .D(and_11_out), .Q(d_ff_11_q));  // open: Qn, preset, en, reset
  D_Flip_Flop d_ff_12 (.clk(CLK), .D(and_12_out), .Q(d_ff_12_q));  // open: Qn, preset, en, reset
  D_Flip_Flop d_ff_13 (.clk(CLK), .D(and_13_out), .Q(d_ff_13_q));  // open: Qn, preset, en, reset
  D_Flip_Flop d_ff_14 (.clk(CLK), .D(and_14_out), .Q(d_ff_14_q));  // open: Qn, preset, en, reset
  and and_15 (K0_VALID, d_ff_1_q, ~in_2[0], ~x_out);  // AND_Gate
  and and_16 (K1_VALID, d_ff_2_q, ~in_2[1], ~x_2_out);  // AND_Gate
  and and_17 (K2_VALID, d_ff_3_q, ~in_2[2], ~x_3_out);  // AND_Gate
  and and_18 (K3_VALID, d_ff_4_q, ~in_2[3], ~x_4_out);  // AND_Gate
  and and_19 (K4_VALID, d_ff_5_q, ~in_2[4], ~x_5_out);  // AND_Gate
  and and_20 (K5_VALID, d_ff_6_q, ~in_2[5], ~x_6_out);  // AND_Gate
  and and_21 (K6_VALID, d_ff_7_q, ~in_2[6], ~x_7_out);  // AND_Gate
  and and_22 (K7_VALID, d_ff_8_q, ~in_2[7], ~x_8_out);  // AND_Gate
  and and_23 (K8_VALID, d_ff_9_q, ~in_2[8], ~x_9_out);  // AND_Gate
  and and_24 (K9_VALID, d_ff_10_q, ~in_2[9], ~x_10_out);  // AND_Gate
  and and_25 (KS_VALID, d_ff_11_q, ~in_2[10], ~x_11_out);  // AND_Gate
  and and_26 (KL_VALID, d_ff_12_q, ~in_2[11], ~x_12_out);  // AND_Gate
  and and_27 (KU_VALID, d_ff_13_q, ~in_2[12], ~x_13_out);  // AND_Gate
  and and_28 (KP_VALID, d_ff_14_q, ~in_2[13], ~x_14_out);  // AND_Gate
  Comparator #(.width(4), .mode("unsigned")) comparator_1 (
    .a(bitadder_1_out), .b(4'b0001), .gt(comparator_1_gt));  // open: eq, lt
  nor nor_1 (nor_1_out, K0_VALID, K1_VALID, K2_VALID, K3_VALID, K4_VALID, K5_VALID, K6_VALID, K7_VALID, K8_VALID, K9_VALID, KS_VALID, KL_VALID, KU_VALID, KP_VALID);
  D_Flip_Flop d_ff_15 (.clk(CLK), .D(comparator_1_gt), .Q(INVALID));  // open: Qn, preset, en, reset
  and and_29 (NO_KEY, nor_1_out, ~INVALID);  // AND_Gate
  or or_1 (or_1_out, K1_VALID, K2_VALID, K3_VALID, K4_VALID, K5_VALID, K6_VALID, K7_VALID, K8_VALID, K9_VALID, K0_VALID);
  Priority_Encoder #(.select(4)) priority_encoder_1 (
    .in0(K0_VALID), .in1(K1_VALID), .in2(K2_VALID), .in3(K3_VALID), .in4(K4_VALID), .in5(K5_VALID),
    .in6(K6_VALID), .in7(K7_VALID), .in8(K8_VALID), .in9(K9_VALID), .in10(KS_VALID), .in11(KL_VALID),
    .in12(KU_VALID), .in13(KP_VALID), .in14(INVALID), .in15(NO_KEY), .out(priority_encoder_1_out));  // open: gs, en_out, en_in
  Shift_Register #(.width(4), .length(3)) shift_register_1 (
    .shift(or_1_out), .in(multiplexer_1_out), .clk(CLK), .clr(or_2_out), .q0(shift_register_1_q0),
    .q1(shift_register_1_q1), .q2(shift_register_1_q2));  // open: out, load, d0, d1, d2
  Multiplexer #(.select(4), .width(4)) multiplexer_1 (
    .in0(4'b0000), .in1(4'b0001), .in2(4'b0010), .in3(4'b0011), .in4(4'b0100), .in5(4'b0101), .in6(4'b0110),
    .in7(4'b0111), .in8(4'b1000), .in9(4'b1001), .in10(undriven), .in11(undriven_4), .in12(undriven_2),
    .in13(undriven_5), .in14(undriven_3), .in15(undriven_6), .out(multiplexer_1_out),
    .sel(priority_encoder_1_out));  // open: en
  or or_2 (or_2_out, KS_VALID, INVALID);
  or or_3 (or_3_out, CORRECT, RST);
  Register #(.width(4)) register_1 (.D(multiplexer_2_out), .en(or_3_out), .Q(register_1_q), .clk(CLK));  // open: clr
  Register #(.width(4)) register_2 (.D(multiplexer_3_out), .en(or_3_out), .Q(register_2_q), .clk(CLK));  // open: clr
  Register #(.width(4)) register_3 (.D(multiplexer_4_out), .en(or_3_out), .Q(register_3_q), .clk(CLK));  // open: clr
  Multiplexer #(.width(4)) multiplexer_2 (
    .in0(4'b0011), .in1(NEW1), .out(multiplexer_2_out), .sel(CORRECT));  // open: en
  Comparator #(.width(4), .mode("unsigned")) comparator_2 (
    .a(shift_register_1_q0), .b(shift_register_2_q0), .eq(comparator_2_eq));  // open: gt, lt
  Comparator #(.width(4), .mode("unsigned")) comparator_3 (
    .a(shift_register_1_q1), .b(shift_register_2_q1), .eq(comparator_3_eq));  // open: gt, lt
  Comparator #(.width(4), .mode("unsigned")) comparator_4 (
    .a(shift_register_1_q2), .b(shift_register_2_q2), .eq(comparator_4_eq));  // open: gt, lt
  Multiplexer #(.width(4)) multiplexer_3 (
    .in0(4'b0001), .in1(NEW2), .out(multiplexer_3_out), .sel(CORRECT));  // open: en
  Shift_Register #(.width(4), .length(3)) shift_register_2 (
    .clk(CLK), .load(1'b1), .d0(register_3_q), .q0(shift_register_2_q0), .d1(register_2_q),
    .q1(shift_register_2_q1), .d2(register_1_q), .q2(shift_register_2_q2));  // open: shift, in, out, clr
  and and_30 (match, comparator_2_eq, comparator_3_eq, comparator_4_eq);
  Multiplexer #(.width(4)) multiplexer_4 (
    .in0(4'b0100), .in1(NEW3), .out(multiplexer_4_out), .sel(CORRECT));  // open: en
endmodule

module ec_fsm_neat (
  input  CLK,
  input  RST,
  input  match,
  input  K0,
  input  K1,
  input  K2,
  input  K3,
  input  K4,
  input  K5,
  input  K6,
  input  K7,
  input  K8,
  input  K9,
  input  KS,
  input  KL,
  input  KU,
  input  KP,
  input  INVALID,
  input  NO_KEY,
  output CORRECT,
  output [3:0] NEW1,
  output [3:0] NEW2,
  output [3:0] NEW3,
  output LOCK_CMD,
  output LOCK_ACT,
  output LEDR,
  output LEDB
);

  wire and_1_out, and_2_out, and_3_out, and_4_out, and_7_out, and_8_out, and_9_out, and_10_out, and_11_out,
       and_12_out, and_13_out, and_14_out, and_15_out, and_16_out, and_17_out, and_18_out, and_19_out,
       and_21_out, and_22_out, and_23_out, and_24_out, and_26_out, and_30_out, and_31_out, and_32_out,
       and_33_out, and_34_out, and_35_out, and_36_out, and_37_out, and_38_out, and_39_out, and_40_out,
       and_41_out, and_42_out, and_43_out, and_44_out, and_45_out, and_46_out, and_47_out, and_48_out,
       and_49_out, and_50_out, and_51_out, and_52_out, and_53_out, and_54_out, and_55_out, COMP1,
       comparator_1_eq, comparator_2_eq, comparator_3_eq, comparator_4_eq, comparator_5_eq, comparator_6_eq,
       comparator_7_eq, comparator_8_eq, comparator_9_eq, CORRECT_t, FAIL, FAIL2, FAIL3, I_OR_NK, K, NS0,
       NS0_U, NS1, NS1_U_M, NS2, NS2_4, NS3, NS4, NS5, NS5_16, NS5_17, NS6, NS7, NS8, NS9, NS10, NS11, NS12,
       NS13, NS14, NS15, NS16, NS17, NS18, or_3_out, or_4_out, or_5_out, or_6_out, or_7_out, or_8_out,
       or_9_out, or_10_out, or_12_out, or_13_out, or_14_out, or_17_out, or_18_out, or_20_out, or_21_out,
       or_23_out, or_25_out, or_27_out, or_28_out, or_29_out, or_30_out, or_31_out, or_32_out, or_33_out,
       or_34_out, or_35_out, or_36_out, or_37_out, or_38_out, or_39_out, SCS, u_match_prime_out;
  wire [3:0] multiplexer_1_out, priority_encoder_1_out, shift_register_1_q0, shift_register_1_q1,
       shift_register_1_q2, shift_register_1_q3, shift_register_1_q4, shift_register_1_q5,
       shift_register_2_q0, shift_register_2_q1, shift_register_2_q2, undriven, undriven_2, undriven_3,
       undriven_4, undriven_5, undriven_6;

  Priority_Encoder #(.select(4)) priority_encoder_1 (
    .in0(K0), .in1(K1), .in2(K2), .in3(K3), .in4(K4), .in5(K5), .in6(K6), .in7(K7), .in8(K8), .in9(K9),
    .in10(KS), .in11(KL), .in12(KU), .in13(KP), .in14(INVALID), .in15(NO_KEY), .out(priority_encoder_1_out));  // open: gs, en_out, en_in
  and and_1 (and_1_out, NS4, ~KS);  // AND_Gate
  and u_match_prime (u_match_prime_out, KU, ~match);  // AND_Gate
  or or_1 (K, K0, K1, K2, K3, K4, K5, K6, K7, K8, K9);
  and and_2 (and_2_out, NS0, I_OR_NK);
  or or_2 (I_OR_NK, INVALID, NO_KEY);
  or or_3 (or_3_out, NS5, NS6, NS7, NS8, NS9, NS10);
  Multiplexer #(.select(4), .width(4)) multiplexer_1 (
    .in0(4'b0000), .in1(4'b0001), .in2(4'b0010), .in3(4'b0011), .in4(4'b0100), .in5(4'b0101), .in6(4'b0110),
    .in7(4'b0111), .in8(4'b1000), .in9(4'b1001), .in10(undriven), .in11(undriven_4), .in12(undriven_2),
    .in13(undriven_5), .in14(undriven_3), .in15(undriven_6), .out(multiplexer_1_out),
    .sel(priority_encoder_1_out));  // open: en
  or or_4 (or_4_out, NS11, NS12, NS13);
  and and_3 (and_3_out, or_4_out, K);
  or or_5 (or_5_out, NS14, NS15, NS16);
  and and_4 (and_4_out, or_5_out, K);
  and and_5 (NS1_U_M, match, KU, NS1);
  or or_6 (or_6_out, u_match_prime_out, KP, KL);
  and and_6 (COMP1, or_6_out, NS1);
  and and_7 (and_7_out, NS3, ~KS);  // AND_Gate
  and and_8 (and_8_out, NS2, ~KS);  // AND_Gate
  and b0_L (LOCK_CMD, KL, NS0);
  or or_7 (or_7_out, NS1, NS0);
  or or_8 (or_8_out, KS, and_2_out);
  and and_9 (and_9_out, or_3_out, K);
  Shift_Register #(.width(4), .length(6)) shift_register_1 (
    .shift(and_9_out), .in(multiplexer_1_out), .clk(CLK), .q0(shift_register_1_q0), .q1(shift_register_1_q1),
    .q2(shift_register_1_q2), .q3(shift_register_1_q3), .q4(shift_register_1_q4), .q5(shift_register_1_q5));  // open: out, load, clr, d0, d1, d2, d3, d4, d5
  Shift_Register #(.width(4), .length(3)) shift_register_2 (
    .shift(and_3_out), .in(multiplexer_1_out), .clk(CLK), .q0(shift_register_2_q0), .q1(shift_register_2_q1),
    .q2(shift_register_2_q2));  // open: out, load, clr, d0, d1, d2
  Shift_Register #(.width(4), .length(3)) shift_register_3 (
    .shift(and_4_out), .in(multiplexer_1_out), .clk(CLK), .q0(NEW3), .q1(NEW2), .q2(NEW1));  // open: out, load, clr, d0, d1, d2
  and and_10 (and_10_out, NS4, I_OR_NK);
  and b_prime___u (NS0_U, KU, NS0);
  and and_11 (and_11_out, K, or_7_out);
  or or_9 (or_9_out, K, I_OR_NK);
  or or_10 (or_10_out, and_10_out, and_1_out, NS1_U_M);
  and and_12 (and_12_out, NS2, I_OR_NK);
  and and_13 (and_13_out, I_OR_NK, NS1);
  or or_11 (LOCK_ACT, LOCK_CMD, NS1_U_M);
  or or_12 (or_12_out, or_9_out, KS);
  or or_13 (or_13_out, NS0, NS1);
  Comparator #(.width(4), .mode("unsigned")) comparator_1 (
    .a(shift_register_1_q5), .b(4'b0001), .eq(comparator_1_eq));  // open: gt, lt
  Comparator #(.width(4), .mode("unsigned")) comparator_2 (
    .a(shift_register_1_q4), .b(4'b0110), .eq(comparator_2_eq));  // open: gt, lt
  Comparator #(.width(4), .mode("unsigned")) comparator_3 (
    .a(shift_register_1_q3), .b(4'b0001), .eq(comparator_3_eq));  // open: gt, lt
  Comparator #(.width(4), .mode("unsigned")) comparator_4 (
    .a(shift_register_1_q2), .b(4'b1000), .eq(comparator_4_eq));  // open: gt, lt
  Comparator #(.width(4), .mode("unsigned")) comparator_5 (
    .a(shift_register_1_q1), .b(4'b0000), .eq(comparator_5_eq));  // open: gt, lt
  Comparator #(.width(4), .mode("unsigned")) comparator_6 (
    .a(shift_register_1_q0), .b(4'b0011), .eq(comparator_6_eq));  // open: gt, lt
  Comparator #(.width(4), .mode("unsigned")) comparator_7 (
    .a(shift_register_2_q2), .b(NEW1), .eq(comparator_7_eq));  // open: gt, lt
  Comparator #(.width(4), .mode("unsigned")) comparator_8 (
    .a(shift_register_2_q1), .b(NEW2), .eq(comparator_8_eq));  // open: gt, lt
  Comparator #(.width(4), .mode("unsigned")) comparator_9 (
    .a(shift_register_2_q0), .b(NEW3), .eq(comparator_9_eq));  // open: gt, lt
  and and_14 (and_14_out, NS3, I_OR_NK);
  or or_14 (or_14_out, and_13_out, and_11_out);
  or or_15 (NS2_4, NS4, NS3, NS2);
  and and_15 (and_15_out, NS3, ~KS);  // AND_Gate
  and and_16 (and_16_out, or_12_out, or_13_out);
  or or_16 (NS5_16, NS5, NS6, NS7, NS8, NS9, NS10, NS11, NS12, NS13, NS14, NS15, NS16);
  and and_17 (and_17_out, comparator_1_eq, comparator_2_eq, comparator_3_eq, comparator_4_eq, comparator_5_eq, comparator_6_eq);
  and and_18 (and_18_out, comparator_7_eq, comparator_8_eq, comparator_9_eq);
  or or_17 (or_17_out, and_14_out, COMP1, FAIL3, NS0_U, and_7_out);
  or or_18 (or_18_out, RST, LOCK_CMD, and_8_out, SCS, and_12_out);
  and and_19 (and_19_out, NS2_4, KS);
  or or_19 (NS5_17, NS5_16, NS17);
  or or_20 (or_20_out, KU, INVALID, KL);
  and and_20 (CORRECT_t, and_17_out, and_18_out);
  D_Flip_Flop u_NS4 (.clk(CLK), .D(or_10_out), .Q(NS4));  // open: Qn, preset, en, reset
  D_Flip_Flop u_NS3 (.clk(CLK), .D(or_17_out), .Q(NS3));  // open: Qn, preset, en, reset
  D_Flip_Flop u_NS2 (.clk(CLK), .D(or_18_out), .Q(NS2));  // open: Qn, preset, en, reset
  D_Flip_Flop u_NS1 (.clk(CLK), .D(or_14_out), .Q(NS1));  // open: Qn, preset, en, reset
  D_Flip_Flop u_NS0 (.clk(CLK), .D(or_8_out), .Q(NS0));  // open: Qn, preset, en, reset
  and and_21 (and_21_out, NS17, K);
  or or_21 (or_21_out, NS0, NS18, NS5_17);
  and and_22 (and_22_out, NS17, K);
  and and_23 (and_23_out, NS5_17, or_20_out);
  and and_24 (and_24_out, NS18, ~KS, ~KP);  // AND_Gate
  and and_25 (CORRECT, KP, NS17, CORRECT_t);
  or or_22 (LEDR, NS0_U, FAIL2, COMP1, FAIL, and_15_out);
  and and_26 (and_26_out, or_21_out, ~KP);  // AND_Gate
  or or_23 (or_23_out, and_22_out, and_23_out, and_24_out);
  or or_24 (LEDB, and_21_out, and_16_out, and_19_out, and_26_out);
  D_Flip_Flop u_NS18 (.clk(CLK), .D(or_23_out), .Q(NS18));  // open: Qn, preset, en, reset
  or or_25 (or_25_out, NS5_16, NS18);
  and and_27 (FAIL2, or_25_out, KP);
  and and_28 (FAIL, NS17, KP, ~CORRECT_t);  // AND_Gate
  and and_29 (SCS, KP, NS17, CORRECT_t);
  and and_30 (and_30_out, NS0, KP);
  and and_31 (and_31_out, NS5, K);
  and and_32 (and_32_out, NS6, K);
  and and_33 (and_33_out, NS7, K);
  and and_34 (and_34_out, NS8, K);
  and and_35 (and_35_out, NS9, K);
  and and_36 (and_36_out, NS10, K);
  and and_37 (and_37_out, NS11, K);
  and and_38 (and_38_out, NS12, K);
  and and_39 (and_39_out, NS13, K);
  and and_40 (and_40_out, NS14, K);
  and and_41 (and_41_out, NS15, K);
  and and_42 (and_42_out, NS16, K);
  and and_43 (and_43_out, NS5, NO_KEY);
  and and_44 (and_44_out, NS6, NO_KEY);
  and and_45 (and_45_out, NS7, NO_KEY);
  and and_46 (and_46_out, NS8, NO_KEY);
  and and_47 (and_47_out, NS9, NO_KEY);
  and and_48 (and_48_out, NS10, NO_KEY);
  and and_49 (and_49_out, NS11, NO_KEY);
  and and_50 (and_50_out, NS12, NO_KEY);
  and and_51 (and_51_out, NS13, NO_KEY);
  and and_52 (and_52_out, NS14, NO_KEY);
  and and_53 (and_53_out, NS15, NO_KEY);
  and and_54 (and_54_out, NS16, NO_KEY);
  and and_55 (and_55_out, NS17, NO_KEY);
  or or_26 (FAIL3, FAIL2, FAIL);
  or or_27 (or_27_out, and_30_out, and_43_out);
  or or_28 (or_28_out, and_31_out, and_44_out);
  or or_29 (or_29_out, and_32_out, and_45_out);
  or or_30 (or_30_out, and_33_out, and_46_out);
  or or_31 (or_31_out, and_34_out, and_47_out);
  or or_32 (or_32_out, and_35_out, and_48_out);
  or or_33 (or_33_out, and_36_out, and_49_out);
  or or_34 (or_34_out, and_37_out, and_50_out);
  or or_35 (or_35_out, and_38_out, and_51_out);
  or or_36 (or_36_out, and_39_out, and_52_out);
  or or_37 (or_37_out, and_40_out, and_53_out);
  or or_38 (or_38_out, and_41_out, and_54_out);
  or or_39 (or_39_out, and_42_out, and_55_out);
  D_Flip_Flop u_NS5 (.clk(CLK), .D(or_27_out), .Q(NS5));  // open: Qn, preset, en, reset
  D_Flip_Flop u_NS6 (.clk(CLK), .D(or_28_out), .Q(NS6));  // open: Qn, preset, en, reset
  D_Flip_Flop u_NS7 (.clk(CLK), .D(or_29_out), .Q(NS7));  // open: Qn, preset, en, reset
  D_Flip_Flop u_NS8 (.clk(CLK), .D(or_30_out), .Q(NS8));  // open: Qn, preset, en, reset
  D_Flip_Flop u_NS9 (.clk(CLK), .D(or_31_out), .Q(NS9));  // open: Qn, preset, en, reset
  D_Flip_Flop u_NS10 (.clk(CLK), .D(or_32_out), .Q(NS10));  // open: Qn, preset, en, reset
  D_Flip_Flop u_NS11 (.clk(CLK), .D(or_33_out), .Q(NS11));  // open: Qn, preset, en, reset
  D_Flip_Flop u_NS12 (.clk(CLK), .D(or_34_out), .Q(NS12));  // open: Qn, preset, en, reset
  D_Flip_Flop u_NS13 (.clk(CLK), .D(or_35_out), .Q(NS13));  // open: Qn, preset, en, reset
  D_Flip_Flop u_NS14 (.clk(CLK), .D(or_36_out), .Q(NS14));  // open: Qn, preset, en, reset
  D_Flip_Flop u_NS15 (.clk(CLK), .D(or_37_out), .Q(NS15));  // open: Qn, preset, en, reset
  D_Flip_Flop u_NS16 (.clk(CLK), .D(or_38_out), .Q(NS16));  // open: Qn, preset, en, reset
  D_Flip_Flop u_NS17 (.clk(CLK), .D(or_39_out), .Q(NS17));  // open: Qn, preset, en, reset

  // Other names for the same wires on the sheet: _0 = K0; _1 = K1; _2 = K2; _3 = K3; _4 = K4; _5 = K5; _6 = K6;
  //   _7 = K7; _8 = K8; _9 = K9; L = KL; M = match; NS0_L = LOCK_CMD; P = KP; S = KS; U = KU
endmodule
