// Logisim project LockTB.circ as structural Verilog: 2 circuits, main circuit LockTB
module LockTB (
);

  wire CLK, d_ff_1_q, K0, K1, K2, K3, K4, K5, K6, K7, K8, K9, KL, KP, KS, KU, LEDB_ON, LEDR_ON, LOCK_ACT,
       LOCK_CMD, RST;
  wire [6:0] multiplexer_1_out;

  Clock u_CLK (.out(CLK));
  Button _1 (.out(K1));
  Button _6 (.out(K6));
  Button P (.out(KP));
  PWRONRST pwronrst_1 (.CLK(CLK), .RST(RST));
  Button S (.out(KS));
  Button _3 (.out(K3));
  Button _2 (.out(K2));
  Button _8 (.out(K8));
  Button _7 (.out(K7));
  Button L (.out(KL));
  Button _4 (.out(K4));
  Button _9 (.out(K9));
  Button U (.out(KU));
  Button _5 (.out(K5));
  Button _0 (.out(K0));
  // LockController lockcontroller_1: pin names not known; wires that end beside it: CLK, RST, K0, K1, K2, K3, K4, K5, K6, K7, K8, K9, KS, KL, KU, KP, LEDB_ON, LEDR_ON, LOCK_ACT, LOCK_CMD
  LED B (.in(LEDB_ON));
  LED R (.in(LEDR_ON));
  Multiplexer #(.width(7)) multiplexer_1 (
    .in0(7'b1110101), .in1(7'b0110100), .out(multiplexer_1_out), .sel(d_ff_1_q));  // open: en
  _7_Segment_Display u_7_segment_display_1 (
    .g(multiplexer_1_out[3]), .f(multiplexer_1_out[2]), .a(multiplexer_1_out[1]), .b(multiplexer_1_out[0]),
    .e(multiplexer_1_out[4]), .d(multiplexer_1_out[5]), .c(multiplexer_1_out[6]));  // open: dp
  D_Flip_Flop d_ff_1 (.clk(CLK), .D(LOCK_CMD), .Q(d_ff_1_q), .en(LOCK_ACT));  // open: Qn, preset, reset

  // Notes on the sheet:
  //   Put you module below and wire it up!
  //   LOCK STATUS
endmodule

module PWRONRST (
  input  CLK,
  output RST
);

  wire d_ff_1_q, nor_1_out, not_1_out;

  not not_1 (not_1_out, nor_1_out);
  D_Flip_Flop d_ff_1 (.clk(CLK), .D(not_1_out), .Q(d_ff_1_q));  // open: Qn, preset, en, reset
  nor nor_1 (nor_1_out, d_ff_1_q, RST);
  D_Flip_Flop d_ff_2 (.clk(CLK), .D(nor_1_out), .Q(RST));  // open: Qn, preset, en, reset

  // Notes on the sheet:
  //   This circuit sets RST=1 for one clock cycle at the beginning and then 0 afterwards.
endmodule
